# Fritzing sketch BeachSafety_v2_reciever (saved by Fritzing 0.9.3b)

parts:
  Part1 = Arduino Nano (Rev3.0)
  VCC1 = Battery  # not connected
  Part4 = NRF905 Stub [chip_label=NRF905 package=SO]
  Part5 = Arduino Nano (Rev3.0) (ICSP)
  U2 = UBLOX NEO 6M GPS
  MPU9250/1 = SparkFun IMU Breakout - MPU-9250

nets:
  N1: Part1.D3, Part4.PW_UP
  N2: Part1.D4, Part4.TRAXCE
  N3: Part1.D5, Part4.TXEN
  N4: Part1.D7, Part4.CD
  N5: Part1.D8, Part4.DR
  N6: Part1.D9, Part4.AM
  N7: Part1.D10, Part4.CSN
  N8: Part1.D11/MOSI, Part4.MOSI
  N9: Part1.D12/MISO, Part4.MISO
  N10: Part1.GND, Part4.GND_13, Part4.GND_14
  3V3: Part1.3V3, Part4.VCC
  N11: Part1.D13/SCK, Part4.SCK
  N12: Part5.D8, U2.TXD, U2.GND
  N13: Part5.D9, U2.RXD
  GND: Part5.GND, MPU9250/1.GND
  N14: Part5.A5, MPU9250/1.SCL
  N15: Part5.A4, MPU9250/1.SDA
  VCC: Part5.3V3, U2.VCC, MPU9250/1.VCC

notes:
  http://www.electrodragon.com/w/NRF905
  https://github.com/athombv/homey-arduino-nrf905/blob/master/doc/arduino_nRF905_wiring.png

custom parts:
  NRF905 Stub: A stub graphic for the NRF905 RF so I can get this project done. The graphic does not look like the product, but it has the correct number of pins in the correct order.
  UBLOX NEO 6M GPS: uSD module
  SparkFun IMU Breakout - MPU-9250: HiLetgo® MPU9250/6500 9-Axis 9 DOF 16 Bit Gyroscope Acceleration Magnetic Sensor 9-Axis Attitude +Gyro+Accelerator+Magnetometer Sensor Module IIC/SPI for Arduino GY-9250
